# Fritzing sketch UNO_PWMout (saved by Fritzing 0.8.3b)
breadboards: 1

parts:
  Součástka1 = Arduino Uno (Rev3)
  R3 = Resistor [tolerance=±5% resistance=220 package=THT]
  LED1 = LED - 3mm [color="Yellow (595nm)" package="3 mm [THT]"]
  LED3 = LED - 3mm [color="Yellow (595nm)" package="3 mm [THT]"]
  R4 = Resistor [tolerance=±5% resistance=220 package=THT]
  LED4 = LED - 3mm [color="Yellow (595nm)" package="3 mm [THT]"]
  R5 = Resistor [tolerance=±5% resistance=220 package=THT]
  LED5 = LED - 3mm [color="Yellow (595nm)" package="3 mm [THT]"]
  LED6 = LED - 3mm [color="Yellow (595nm)" package="3 mm [THT]"]
  R6 = Resistor [tolerance=±5% resistance=220 package=THT]
  R7 = Resistor [tolerance=±5% resistance=220 package=THT]

nets:
  N1: Součástka1.GND, R3.Pin_1, R4.Pin_1, R5.Pin_1, R6.Pin_1, R7.Pin_1
  N2: Součástka1.D9_PWM, LED4.anode
  N3: Součástka1.D10_PWM/SS, LED3.anode
  N4: Součástka1.D11_PWM/MOSI, LED1.anode
  N5: Součástka1.D5_PWM, LED5.anode
  N6: Součástka1.D6_PWM, LED6.anode
  N7: R3.Pin_0, LED1.cathode
  N8: LED3.cathode, R5.Pin_0
  N9: R4.Pin_0, LED4.cathode
  N10: LED5.cathode, R6.Pin_0
  N11: LED6.cathode, R7.Pin_0
