# Fritzing sketch X_UNO_Blink (saved by Fritzing 0.8.3b)
breadboards: 1

parts:
  Součástka1 = Arduino Uno (Rev3)
  R3 = Resistor [tolerance=±5% resistance=220 package=THT]
  LED1 = LED - 3mm [color="Red (633nm)" package="3 mm [THT]"]
  LED3 = LED - 3mm [color="Yellow (595nm)" package="3 mm [THT]"]
  R4 = Resistor [tolerance=±5% resistance=220 package=THT]
  LED4 = LED - 3mm [color="Green (555nm)" package="3 mm [THT]"]
  R5 = Resistor [tolerance=±5% resistance=220 package=THT]

nets:
  N1: Součástka1.GND, R3.Pin_1, R4.Pin_1, R5.Pin_1
  N2: Součástka1.D9_PWM, LED4.anode
  N3: Součástka1.D10_PWM/SS, LED3.anode
  N4: Součástka1.D11_PWM/MOSI, LED1.anode
  N5: R3.Pin_0, LED1.cathode
  N6: LED3.cathode, R5.Pin_0
  N7: R4.Pin_0, LED4.cathode
